# Fritzing sketch wiring (saved by Fritzing 0.9.3b)
breadboards: 1

parts:
  Bauteil1 = Arduino Nano (Rev3.0) (ICSP)
  DI1 = 7-Segment LED Display [package=THT]
  DI2 = 7-Segment LED Display [package=THT]
  Q1 = Basic FET N-Channel [package="D2Pak [SMD]"]
  Q2 = Basic FET N-Channel [package="D2Pak [SMD]"]
  hc-sr1 = hc-sr04
  R1 = Resistor [tolerance=±5% resistance=220 package="1206 [SMD]"]
  R2 = Resistor [tolerance=±5% resistance=220 package="1206 [SMD]"]

nets:
  GND: Bauteil1.GND, Q1.source, Q2.source, hc-sr1.GND
  N1: Bauteil1.D2, DI2.cathodeG
  N2: Bauteil1.D3, DI2.cathodeF
  N3: Bauteil1.D4, DI2.cathodeE
  N4: Bauteil1.D5, DI2.cathodeD
  N5: Bauteil1.D6, DI2.cathodeC
  N6: Bauteil1.D7, DI2.cathodeB
  N7: Bauteil1.D8, DI2.cathodeA
  N8: Bauteil1.D9, Q1.Gate
  N9: Bauteil1.D10, Q2.Gate
  N10: Bauteil1.D11/MOSI, hc-sr1.Echo
  N11: Bauteil1.D12/MISO, hc-sr1.Trig
  5V: Bauteil1.5V, hc-sr1.VCC
  N12: DI1.commAnode#2, R2.Pin_0
  N13: DI2.commAnode#2, R1.Pin_0
  N14: Q1.drain, R2.Pin_1
  N15: Q2.drain, R1.Pin_1
